// Logisim project 2307080_ALU_MD.circ as structural Verilog: 11 circuits, main circuit main CKT
// alu booth
module main_CKT (
  input  [2:0] Control,
  input  [27:0] A,
  input  [27:0] B,
  output [27:0] Result_01,
  output [27:0] Result_02__C,
  output Zero,
  output Negative,
  output Overflow,
  output Carry
);

  _28_bit_ALU_with_booth u_28_bit_alu_with_booth_1 (
    .A(A), .B(B), .Result_02(Result_02__C), .Zero(Zero), .Negative(Negative), .Overflow(Overflow),
    .Carry(Carry), .Control0(Control[0]), .Control2(Control[2]), .Control1(Control[1]));  // open: Result_01

  // Notes on the sheet:
  //   001- ADDITION
  //   101- DIVISION
  //   000 - AND OPERATION
  //   010 - OR OPERATION
  //   011- SUBTRACTION
  //   100- MULTIPLICATION
endmodule

// 28-bit AND
module _28_bit_and (
  input  [27:0] A,
  input  [27:0] B,
  output [27:0] Result
);

  and and_1 (Result[0], B[0], A[0]);
  and and_2 (Result[1], B[1], A[1]);
  and and_3 (Result[2], B[2], A[2]);
  and and_4 (Result[3], B[3], A[3]);
  and and_5 (Result[4], A[4], B[4]);
  and and_6 (Result[5], A[5], B[5]);
  and and_7 (Result[6], A[6], B[6]);
  and and_8 (Result[7], A[7], B[7]);
  and and_9 (Result[8], A[8], B[8]);
  and and_10 (Result[9], A[9], B[9]);
  and and_11 (Result[10], A[10], B[10]);
  and and_12 (Result[11], A[11], B[11]);
  and and_13 (Result[12], A[12], B[12]);
  and and_14 (Result[13], A[13], B[13]);
  and and_15 (Result[14], A[14], B[14]);
  and and_16 (Result[15], A[15], B[15]);
  and and_17 (Result[16], A[16], B[16]);
  and and_18 (Result[17], A[17], B[17]);
  and and_19 (Result[18], A[18], B[18]);
  and and_20 (Result[19], A[19], B[19]);
  and and_21 (Result[20], A[20], B[21]);
  and and_22 (Result[21], A[21], B[20]);
  and and_23 (Result[22], A[22], B[22]);
  and and_24 (Result[23], A[23], B[23]);
  and and_25 (Result[24], A[24], B[24]);
  and and_26 (Result[25], A[25], B[25]);
  and and_27 (Result[26], A[26], B[26]);
  and and_28 (Result[27], A[27], B[27]);
endmodule

// 28-bit OR
module _28_bit_OR (
  input  [27:0] A,
  input  [27:0] B,
  output [27:0] Result
);

  or or_1 (Result[0], B[0], A[0]);
  or or_2 (Result[1], B[1], A[1]);
  or or_3 (Result[2], B[2], A[2]);
  or or_4 (Result[3], B[3], A[3]);
  or or_5 (Result[4], A[4], B[4]);
  or or_6 (Result[5], A[5], B[5]);
  or or_7 (Result[6], A[6], B[6]);
  or or_8 (Result[7], A[7], B[7]);
  or or_9 (Result[8], A[8], B[8]);
  or or_10 (Result[9], A[9], B[9]);
  or or_11 (Result[10], A[10], B[10]);
  or or_12 (Result[11], A[11], B[11]);
  or or_13 (Result[12], A[12], B[12]);
  or or_14 (Result[13], A[13], B[13]);
  or or_15 (Result[14], A[14], B[14]);
  or or_16 (Result[15], A[15], B[15]);
  or or_17 (Result[16], A[16], B[16]);
  or or_18 (Result[17], A[17], B[17]);
  or or_19 (Result[18], A[18], B[18]);
  or or_20 (Result[19], A[19], B[19]);
  or or_21 (Result[20], A[20], B[21]);
  or or_22 (Result[21], A[21], B[20]);
  or or_23 (Result[22], A[22], B[22]);
  or or_24 (Result[23], A[23], B[23]);
  or or_25 (Result[24], A[24], B[24]);
  or or_26 (Result[25], A[25], B[25]);
  or or_27 (Result[26], A[26], B[26]);
  or or_28 (Result[27], A[27], B[27]);
endmodule

module Full_adder (
  input  Carry_in,
  input  A,
  input  B,
  output Result,
  output Carry_out
);

  wire and_1_out, and_2_out, xor_1_out;

  and and_1 (and_1_out, B, A);
  xor xor_1 (xor_1_out, A, B);
  or or_1 (Carry_out, and_1_out, and_2_out);
  and and_2 (and_2_out, xor_1_out, Carry_in);
  xor xor_2 (Result, Carry_in, xor_1_out);
endmodule

// FA
module _24_bit_full_adder_concise (
  input  Carry_in,
  input  [27:0] A,
  input  [27:0] B,
  output [27:0] Result,
  output Carry_out
);

  wire full_adder_1_carry_out, full_adder_2_carry_out, full_adder_3_carry_out, full_adder_4_carry_out,
       full_adder_5_carry_out, full_adder_6_carry_out, full_adder_7_carry_out, full_adder_8_carry_out,
       full_adder_9_carry_out, full_adder_10_carry_out, full_adder_11_carry_out, full_adder_12_carry_out,
       full_adder_13_carry_out, full_adder_14_carry_out, full_adder_15_carry_out, full_adder_16_carry_out,
       full_adder_17_carry_out, full_adder_18_carry_out, full_adder_19_carry_out, full_adder_20_carry_out,
       full_adder_21_carry_out, full_adder_22_carry_out, full_adder_23_carry_out, full_adder_24_carry_out,
       full_adder_25_carry_out, full_adder_26_carry_out, full_adder_27_carry_out;

  Full_adder full_adder_1 (
    .Carry_in(Carry_in), .A(B[0]), .B(A[0]), .Result(Result[0]), .Carry_out(full_adder_1_carry_out));
  Full_adder full_adder_2 (
    .Carry_in(full_adder_1_carry_out), .A(B[1]), .B(A[1]), .Result(Result[1]),
    .Carry_out(full_adder_2_carry_out));
  Full_adder full_adder_3 (
    .Carry_in(full_adder_2_carry_out), .A(B[2]), .B(A[2]), .Result(Result[2]),
    .Carry_out(full_adder_3_carry_out));
  Full_adder full_adder_4 (
    .Carry_in(full_adder_3_carry_out), .A(B[3]), .B(A[3]), .Result(Result[3]),
    .Carry_out(full_adder_4_carry_out));
  Full_adder full_adder_5 (
    .Carry_in(full_adder_4_carry_out), .A(A[4]), .B(B[4]), .Result(Result[4]),
    .Carry_out(full_adder_5_carry_out));
  Full_adder full_adder_6 (
    .Carry_in(full_adder_5_carry_out), .A(A[5]), .B(B[5]), .Result(Result[5]),
    .Carry_out(full_adder_6_carry_out));
  Full_adder full_adder_7 (
    .Carry_in(full_adder_6_carry_out), .A(A[6]), .B(B[6]), .Result(Result[6]),
    .Carry_out(full_adder_7_carry_out));
  Full_adder full_adder_8 (
    .Carry_in(full_adder_7_carry_out), .A(A[7]), .B(B[7]), .Result(Result[7]),
    .Carry_out(full_adder_8_carry_out));
  Full_adder full_adder_9 (
    .Carry_in(full_adder_8_carry_out), .A(A[8]), .B(B[8]), .Result(Result[8]),
    .Carry_out(full_adder_9_carry_out));
  Full_adder full_adder_10 (
    .Carry_in(full_adder_9_carry_out), .A(A[9]), .B(B[9]), .Result(Result[9]),
    .Carry_out(full_adder_10_carry_out));
  Full_adder full_adder_11 (
    .Carry_in(full_adder_10_carry_out), .A(A[10]), .B(B[10]), .Result(Result[10]),
    .Carry_out(full_adder_11_carry_out));
  Full_adder full_adder_12 (
    .Carry_in(full_adder_11_carry_out), .A(A[11]), .B(B[11]), .Result(Result[11]),
    .Carry_out(full_adder_12_carry_out));
  Full_adder full_adder_13 (
    .Carry_in(full_adder_12_carry_out), .A(A[12]), .B(B[12]), .Result(Result[12]),
    .Carry_out(full_adder_13_carry_out));
  Full_adder full_adder_14 (
    .Carry_in(full_adder_13_carry_out), .A(A[13]), .B(B[13]), .Result(Result[13]),
    .Carry_out(full_adder_14_carry_out));
  Full_adder full_adder_15 (
    .Carry_in(full_adder_14_carry_out), .A(A[14]), .B(B[14]), .Result(Result[14]),
    .Carry_out(full_adder_15_carry_out));
  Full_adder full_adder_16 (
    .Carry_in(full_adder_15_carry_out), .A(A[15]), .B(B[15]), .Result(Result[15]),
    .Carry_out(full_adder_16_carry_out));
  Full_adder full_adder_17 (
    .Carry_in(full_adder_16_carry_out), .A(A[16]), .B(B[16]), .Result(Result[16]),
    .Carry_out(full_adder_17_carry_out));
  Full_adder full_adder_18 (
    .Carry_in(full_adder_17_carry_out), .A(A[17]), .B(B[17]), .Result(Result[17]),
    .Carry_out(full_adder_18_carry_out));
  Full_adder full_adder_19 (
    .Carry_in(full_adder_18_carry_out), .A(A[18]), .B(B[18]), .Result(Result[18]),
    .Carry_out(full_adder_19_carry_out));
  Full_adder full_adder_20 (
    .Carry_in(full_adder_19_carry_out), .A(A[19]), .B(B[19]), .Result(Result[19]),
    .Carry_out(full_adder_20_carry_out));
  Full_adder full_adder_21 (
    .Carry_in(full_adder_20_carry_out), .A(A[20]), .B(B[21]), .Result(Result[20]),
    .Carry_out(full_adder_21_carry_out));
  Full_adder full_adder_22 (
    .Carry_in(full_adder_21_carry_out), .A(A[21]), .B(B[20]), .Result(Result[21]),
    .Carry_out(full_adder_22_carry_out));
  Full_adder full_adder_23 (
    .Carry_in(full_adder_22_carry_out), .A(A[22]), .B(B[22]), .Result(Result[22]),
    .Carry_out(full_adder_23_carry_out));
  Full_adder full_adder_24 (
    .Carry_in(full_adder_23_carry_out), .A(A[23]), .B(B[23]), .Result(Result[23]),
    .Carry_out(full_adder_24_carry_out));
  Full_adder full_adder_25 (
    .Carry_in(full_adder_24_carry_out), .A(A[24]), .B(B[24]), .Result(Result[24]),
    .Carry_out(full_adder_25_carry_out));
  Full_adder full_adder_26 (
    .Carry_in(full_adder_25_carry_out), .A(A[25]), .B(B[25]), .Result(Result[25]),
    .Carry_out(full_adder_26_carry_out));
  Full_adder full_adder_27 (
    .Carry_in(full_adder_26_carry_out), .A(A[26]), .B(B[26]), .Result(Result[26]),
    .Carry_out(full_adder_27_carry_out));
  Full_adder full_adder_28 (
    .Carry_in(full_adder_27_carry_out), .A(A[27]), .B(B[27]), .Result(Result[27]), .Carry_out(Carry_out));
endmodule

module _28_bit_xor (
  input  Control,
  input  [27:0] B,
  output [27:0] Result
);

  wire [27:0] bit_extender_1_out;

  assign bit_extender_1_out = {{27{Control}}, Control};  // Bit_Extender bit_extender_1
  assign Result = bit_extender_1_out ^ B;  // XOR_Gate xor_1, 28 bits wide
endmodule

// 28-bit \nADD/SUB
module Add_sub (
  input  Sub,
  input  [27:0] A,
  input  [27:0] B,
  output [27:0] Result,
  output Carry,
  output Overflow
);

  wire and_1_out, and_2_out, n27th_bit_out_1__23th_bit, n27th_bit_out_2__23th_bit, n27th_bit_out_3__23th_bit,
       not_1_out, not_2_out, not_3_out;
  wire [27:0] n28_bit_xor_1_result;

  _27th_bit_out u_27th_bit_out_1 (.Input(A), ._23th_bit(n27th_bit_out_1__23th_bit));
  not not_1 (not_1_out, n27th_bit_out_1__23th_bit);
  _27th_bit_out u_27th_bit_out_2 (.Input(B), ._23th_bit(n27th_bit_out_2__23th_bit));
  not not_2 (not_2_out, n27th_bit_out_2__23th_bit);
  _28_bit_xor u_28_bit_xor_1 (.B(B), .Result(n28_bit_xor_1_result), .Control(Sub));
  _24_bit_full_adder_concise u_24_bit_full_adder_concise_1 (
    .A(A), .Result(Result), .B(n28_bit_xor_1_result), .Carry_in(Sub), .Carry_out(Carry));
  _27th_bit_out u_27th_bit_out_3 (.Input(Result), ._23th_bit(n27th_bit_out_3__23th_bit));
  not not_3 (not_3_out, n27th_bit_out_3__23th_bit);
  and and_1 (and_1_out, not_3_out, n27th_bit_out_2__23th_bit, n27th_bit_out_1__23th_bit);
  and and_2 (and_2_out, n27th_bit_out_3__23th_bit, not_2_out, not_1_out);
  or or_1 (Overflow, and_1_out, and_2_out);

  // Notes on the sheet:
  //   A27
  //   B27
  //   Result 27
endmodule

// 27th
module _27th_bit_out (
  input  [27:0] Input,
  output _23th_bit
);


  assign _23th_bit = Input[27];
endmodule

// Reduce-OR
module _28_bit_reduce_or (
  input  [27:0] Input,
  output Output
);

  or or_1 (Output, Input[13], Input[0], Input[1], Input[2], Input[3], Input[4], Input[5], Input[6], Input[7], Input[8], Input[9], Input[10], Input[11], Input[12], Input[14], Input[15], Input[16], Input[17], Input[18], Input[19], Input[20], Input[21], Input[22], Input[23], Input[24], Input[25], Input[26], Input[27]);
endmodule

module _28_bit_ALU_with_booth (
  input  Control1,
  input  Control2,
  input  Control0,
  input  [27:0] A,
  input  [27:0] B,
  output [27:0] Result_01,
  output [27:0] Result_02,
  output Zero,
  output Negative,
  output Overflow,
  output Carry
);

  wire n28_bit_reduce_or_1_output;
  wire [27:0] add_sub_1_result, divider_1_out, multiplier_1_out, n28_bit_and_1_result, n28_bit_or_1_result;

  _28_bit_and u_28_bit_and_1 (.A(A), .Result(n28_bit_and_1_result), .B(B));
  _28_bit_OR u_28_bit_or_1 (.A(A), .Result(n28_bit_or_1_result), .B(B));
  Add_sub add_sub_1 (.Sub(Control0), .A(A), .B(B), .Result(add_sub_1_result), .Carry(Carry), .Overflow(Overflow));
  Multiplier #(.width(28)) multiplier_1 (.a(A), .b(B), .out(multiplier_1_out), .cout(Result_01));  // open: cin
  Divider #(.width(28)) divider_1 (.a(A), .b(B), .out(divider_1_out), .upper(Result_01));  // open: rem
  Multiplexer #(.select(3), .width(28), .enable("false")) multiplexer_1 (
    .in0(n28_bit_and_1_result), .in1(n28_bit_or_1_result), .in2(add_sub_1_result), .in3(add_sub_1_result),
    .in4(multiplier_1_out), .in5(divider_1_out), .in6(divider_1_out), .in7(divider_1_out), .out(Result_02),
    .sel({Control2, Control1, Control0}));
  _27th_bit_out u_27th_bit_out_1 (.Input(Result_02), ._23th_bit(Negative));
  _28_bit_reduce_or u_28_bit_reduce_or_1 (.Input(Result_02), .Output(n28_bit_reduce_or_1_output));
  not not_1 (Zero, n28_bit_reduce_or_1_output);
endmodule

module Booth_MUL (
  input  [27:0] M_input,
  input  [27:0] Q_input,
  input  Reset,
  input  CLKt,
  output [27:0] A_output,
  output [27:0] Q_output
);

  wire A_out, controller_1_c0, controller_1_c1, controller_1_cl__a__q_1, controller_1_dec_cnt,
       controller_1_load__m__q__cnt, controller_1_load_a, controller_1_shr, or_1_out, Q__1_q0, Q_out;
  wire [4:0] counter_1_q;
  wire [27:0] M_q27, n28biit_alu_1_result;

  Controller controller_1 (
    .Clk(CLKt), .Q0(Q_output[0]), .Q_1(Q__1_q0), .Count(counter_1_q), .C0(controller_1_c0),
    .C1(controller_1_c1), .Shr(controller_1_shr), .Dec_Cnt(controller_1_dec_cnt),
    .Cl__A__Q_1(controller_1_cl__a__q_1), .Load_A(controller_1_load_a),
    .LOad__M__Q__Cnt(controller_1_load__m__q__cnt), .Reset(Reset));
  or or_1 (or_1_out, controller_1_load__m__q__cnt, controller_1_dec_cnt);
  Counter #(.width(5), .max('h1f)) counter_1 (
    .load(or_1_out), .D(5'b11100), .count(controller_1_dec_cnt), .Q(counter_1_q), .clk(CLKt));  // open: carry, clr
  Shift_Register #(.length(28)) A (
    .shift(controller_1_shr), .in(A_output[27]), .clk(CLKt), .out(A_out), .load(controller_1_load_a),
    .clr(controller_1_cl__a__q_1), .d0(n28biit_alu_1_result[27]), .q0(A_output[27]),
    .d1(n28biit_alu_1_result[26]), .q1(A_output[26]), .d2(n28biit_alu_1_result[25]), .q2(A_output[25]),
    .d3(n28biit_alu_1_result[24]), .q3(A_output[24]), .d4(n28biit_alu_1_result[23]), .q4(A_output[23]),
    .d5(n28biit_alu_1_result[22]), .q5(A_output[22]), .d6(n28biit_alu_1_result[21]), .q6(A_output[21]),
    .d7(n28biit_alu_1_result[20]), .q7(A_output[20]), .d8(n28biit_alu_1_result[19]), .q8(A_output[19]),
    .d9(n28biit_alu_1_result[18]), .q9(A_output[18]), .d10(n28biit_alu_1_result[17]), .q10(A_output[17]),
    .d11(n28biit_alu_1_result[16]), .q11(A_output[16]), .d12(n28biit_alu_1_result[15]), .q12(A_output[15]),
    .d13(n28biit_alu_1_result[14]), .q13(A_output[14]), .d14(n28biit_alu_1_result[13]), .q14(A_output[13]),
    .d15(n28biit_alu_1_result[12]), .q15(A_output[12]), .d16(n28biit_alu_1_result[11]), .q16(A_output[11]),
    .d17(n28biit_alu_1_result[10]), .q17(A_output[10]), .d18(n28biit_alu_1_result[9]), .q18(A_output[9]),
    .d19(n28biit_alu_1_result[8]), .q19(A_output[8]), .d20(n28biit_alu_1_result[7]), .q20(A_output[7]),
    .d21(n28biit_alu_1_result[6]), .q21(A_output[6]), .d22(n28biit_alu_1_result[5]), .q22(A_output[5]),
    .d23(n28biit_alu_1_result[4]), .q23(A_output[4]), .d24(n28biit_alu_1_result[3]), .q24(A_output[3]),
    .d25(n28biit_alu_1_result[2]), .q25(A_output[2]), .d26(n28biit_alu_1_result[1]), .q26(A_output[1]),
    .d27(n28biit_alu_1_result[0]), .q27(A_output[0]));
  Shift_Register #(.length(28)) M (
    .shift(1'b0), .clk(CLKt), .load(controller_1_load__m__q__cnt), .d0(M_input[27]), .q0(M_q27[27]),
    .d1(M_input[26]), .q1(M_q27[26]), .d2(M_input[25]), .q2(M_q27[25]), .d3(M_input[24]), .q3(M_q27[24]),
    .d4(M_input[23]), .q4(M_q27[23]), .d5(M_input[22]), .q5(M_q27[22]), .d6(M_input[21]), .q6(M_q27[21]),
    .d7(M_input[20]), .q7(M_q27[20]), .d8(M_input[19]), .q8(M_q27[19]), .d9(M_input[18]), .q9(M_q27[18]),
    .d10(M_input[17]), .q10(M_q27[17]), .d11(M_input[16]), .q11(M_q27[16]), .d12(M_input[15]),
    .q12(M_q27[15]), .d13(M_input[14]), .q13(M_q27[14]), .d14(M_input[13]), .q14(M_q27[13]),
    .d15(M_input[12]), .q15(M_q27[12]), .d16(M_input[11]), .q16(M_q27[11]), .d17(M_input[10]),
    .q17(M_q27[10]), .d18(M_input[9]), .q18(M_q27[9]), .d19(M_input[8]), .q19(M_q27[8]), .d20(M_input[7]),
    .q20(M_q27[7]), .d21(M_input[6]), .q21(M_q27[6]), .d22(M_input[5]), .q22(M_q27[5]), .d23(M_input[4]),
    .q23(M_q27[4]), .d24(M_input[3]), .q24(M_q27[3]), .d25(M_input[2]), .q25(M_q27[2]), .d26(M_input[1]),
    .q26(M_q27[1]), .d27(M_input[0]), .q27(M_q27[0]));  // open: in, out, clr
  Shift_Register #(.length(28)) Q (
    .shift(controller_1_shr), .in(A_out), .clk(CLKt), .out(Q_out), .load(controller_1_load__m__q__cnt),
    .d0(Q_input[27]), .q0(Q_output[27]), .d1(Q_input[26]), .q1(Q_output[26]), .d2(Q_input[25]),
    .q2(Q_output[25]), .d3(Q_input[24]), .q3(Q_output[24]), .d4(Q_input[23]), .q4(Q_output[23]),
    .d5(Q_input[22]), .q5(Q_output[22]), .d6(Q_input[21]), .q6(Q_output[21]), .d7(Q_input[20]),
    .q7(Q_output[20]), .d8(Q_input[19]), .q8(Q_output[19]), .d9(Q_input[18]), .q9(Q_output[18]),
    .d10(Q_input[17]), .q10(Q_output[17]), .d11(Q_input[16]), .q11(Q_output[16]), .d12(Q_input[15]),
    .q12(Q_output[15]), .d13(Q_input[14]), .q13(Q_output[14]), .d14(Q_input[13]), .q14(Q_output[13]),
    .d15(Q_input[12]), .q15(Q_output[12]), .d16(Q_input[11]), .q16(Q_output[11]), .d17(Q_input[10]),
    .q17(Q_output[10]), .d18(Q_input[9]), .q18(Q_output[9]), .d19(Q_input[8]), .q19(Q_output[8]),
    .d20(Q_input[7]), .q20(Q_output[7]), .d21(Q_input[6]), .q21(Q_output[6]), .d22(Q_input[5]),
    .q22(Q_output[5]), .d23(Q_input[4]), .q23(Q_output[4]), .d24(Q_input[3]), .q24(Q_output[3]),
    .d25(Q_input[2]), .q25(Q_output[2]), .d26(Q_input[1]), .q26(Q_output[1]), .d27(Q_input[0]),
    .q27(Q_output[0]));  // open: clr
  Shift_Register #(.length(1)) Q__1 (
    .shift(controller_1_shr), .in(Q_out), .clk(CLKt), .clr(controller_1_cl__a__q_1), .q0(Q__1_q0));  // open: out, load, d0
  _28biit_ALU u_28biit_alu_1 (
    .A(A_output), .B(M_q27), .Result(n28biit_alu_1_result), .Control0(controller_1_c0),
    .Control1(controller_1_c1));  // open: Zero, Negative, Overflow, Carry
endmodule
