// Logisim project Booths_multiplication -Copy.circ as structural Verilog: 11 circuits, main circuit Booth's multiplier
module Booth_s_multiplier (
  input  [27:0] M_input,
  input  [27:0] Q_input,
  input  Reset,
  input  CLKt,
  output [27:0] A_output,
  output [27:0] Q_output
);

  wire A_out, controller_1_c0, controller_1_c1, controller_1_cl__a__q_1, controller_1_dec_cnt,
       controller_1_load__m__q__cnt, controller_1_load_a, controller_1_shr, or_1_out, Q__1_q0, Q_out;
  wire [4:0] counter_1_q;
  wire [27:0] M_q27, n28biit_alu_1_result;

  Controller controller_1 (
    .Clk(CLKt), .Q0(Q_output[0]), .Q_1(Q__1_q0), .Count(counter_1_q), .C0(controller_1_c0),
    .C1(controller_1_c1), .Shr(controller_1_shr), .Dec_Cnt(controller_1_dec_cnt),
    .Cl__A__Q_1(controller_1_cl__a__q_1), .Load_A(controller_1_load_a),
    .LOad__M__Q__Cnt(controller_1_load__m__q__cnt), .Reset(Reset));
  or or_1 (or_1_out, controller_1_load__m__q__cnt, controller_1_dec_cnt);
  Counter #(.width(5), .max('h1f)) counter_1 (
    .load(or_1_out), .D(5'b11100), .count(controller_1_dec_cnt), .Q(counter_1_q), .clk(CLKt));  // open: carry, clr
  Shift_Register #(.length(28)) A (
    .shift(controller_1_shr), .in(A_output[27]), .clk(CLKt), .out(A_out), .load(controller_1_load_a),
    .clr(controller_1_cl__a__q_1), .d0(n28biit_alu_1_result[27]), .q0(A_output[27]),
    .d1(n28biit_alu_1_result[26]), .q1(A_output[26]), .d2(n28biit_alu_1_result[25]), .q2(A_output[25]),
    .d3(n28biit_alu_1_result[24]), .q3(A_output[24]), .d4(n28biit_alu_1_result[23]), .q4(A_output[23]),
    .d5(n28biit_alu_1_result[22]), .q5(A_output[22]), .d6(n28biit_alu_1_result[21]), .q6(A_output[21]),
    .d7(n28biit_alu_1_result[20]), .q7(A_output[20]), .d8(n28biit_alu_1_result[19]), .q8(A_output[19]),
    .d9(n28biit_alu_1_result[18]), .q9(A_output[18]), .d10(n28biit_alu_1_result[17]), .q10(A_output[17]),
    .d11(n28biit_alu_1_result[16]), .q11(A_output[16]), .d12(n28biit_alu_1_result[15]), .q12(A_output[15]),
    .d13(n28biit_alu_1_result[14]), .q13(A_output[14]), .d14(n28biit_alu_1_result[13]), .q14(A_output[13]),
    .d15(n28biit_alu_1_result[12]), .q15(A_output[12]), .d16(n28biit_alu_1_result[11]), .q16(A_output[11]),
    .d17(n28biit_alu_1_result[10]), .q17(A_output[10]), .d18(n28biit_alu_1_result[9]), .q18(A_output[9]),
    .d19(n28biit_alu_1_result[8]), .q19(A_output[8]), .d20(n28biit_alu_1_result[7]), .q20(A_output[7]),
    .d21(n28biit_alu_1_result[6]), .q21(A_output[6]), .d22(n28biit_alu_1_result[5]), .q22(A_output[5]),
    .d23(n28biit_alu_1_result[4]), .q23(A_output[4]), .d24(n28biit_alu_1_result[3]), .q24(A_output[3]),
    .d25(n28biit_alu_1_result[2]), .q25(A_output[2]), .d26(n28biit_alu_1_result[1]), .q26(A_output[1]),
    .d27(n28biit_alu_1_result[0]), .q27(A_output[0]));
  Shift_Register #(.length(28)) M (
    .shift(1'b0), .clk(CLKt), .load(controller_1_load__m__q__cnt), .d0(M_input[27]), .q0(M_q27[27]),
    .d1(M_input[26]), .q1(M_q27[26]), .d2(M_input[25]), .q2(M_q27[25]), .d3(M_input[24]), .q3(M_q27[24]),
    .d4(M_input[23]), .q4(M_q27[23]), .d5(M_input[22]), .q5(M_q27[22]), .d6(M_input[21]), .q6(M_q27[21]),
    .d7(M_input[20]), .q7(M_q27[20]), .d8(M_input[19]), .q8(M_q27[19]), .d9(M_input[18]), .q9(M_q27[18]),
    .d10(M_input[17]), .q10(M_q27[17]), .d11(M_input[16]), .q11(M_q27[16]), .d12(M_input[15]),
    .q12(M_q27[15]), .d13(M_input[14]), .q13(M_q27[14]), .d14(M_input[13]), .q14(M_q27[13]),
    .d15(M_input[12]), .q15(M_q27[12]), .d16(M_input[11]), .q16(M_q27[11]), .d17(M_input[10]),
    .q17(M_q27[10]), .d18(M_input[9]), .q18(M_q27[9]), .d19(M_input[8]), .q19(M_q27[8]), .d20(M_input[7]),
    .q20(M_q27[7]), .d21(M_input[6]), .q21(M_q27[6]), .d22(M_input[5]), .q22(M_q27[5]), .d23(M_input[4]),
    .q23(M_q27[4]), .d24(M_input[3]), .q24(M_q27[3]), .d25(M_input[2]), .q25(M_q27[2]), .d26(M_input[1]),
    .q26(M_q27[1]), .d27(M_input[0]), .q27(M_q27[0]));  // open: in, out, clr
  Shift_Register #(.length(28)) Q (
    .shift(controller_1_shr), .in(A_out), .clk(CLKt), .out(Q_out), .load(controller_1_load__m__q__cnt),
    .d0(Q_input[27]), .q0(Q_output[27]), .d1(Q_input[26]), .q1(Q_output[26]), .d2(Q_input[25]),
    .q2(Q_output[25]), .d3(Q_input[24]), .q3(Q_output[24]), .d4(Q_input[23]), .q4(Q_output[23]),
    .d5(Q_input[22]), .q5(Q_output[22]), .d6(Q_input[21]), .q6(Q_output[21]), .d7(Q_input[20]),
    .q7(Q_output[20]), .d8(Q_input[19]), .q8(Q_output[19]), .d9(Q_input[18]), .q9(Q_output[18]),
    .d10(Q_input[17]), .q10(Q_output[17]), .d11(Q_input[16]), .q11(Q_output[16]), .d12(Q_input[15]),
    .q12(Q_output[15]), .d13(Q_input[14]), .q13(Q_output[14]), .d14(Q_input[13]), .q14(Q_output[13]),
    .d15(Q_input[12]), .q15(Q_output[12]), .d16(Q_input[11]), .q16(Q_output[11]), .d17(Q_input[10]),
    .q17(Q_output[10]), .d18(Q_input[9]), .q18(Q_output[9]), .d19(Q_input[8]), .q19(Q_output[8]),
    .d20(Q_input[7]), .q20(Q_output[7]), .d21(Q_input[6]), .q21(Q_output[6]), .d22(Q_input[5]),
    .q22(Q_output[5]), .d23(Q_input[4]), .q23(Q_output[4]), .d24(Q_input[3]), .q24(Q_output[3]),
    .d25(Q_input[2]), .q25(Q_output[2]), .d26(Q_input[1]), .q26(Q_output[1]), .d27(Q_input[0]),
    .q27(Q_output[0]));  // open: clr
  Shift_Register #(.length(1)) Q__1 (
    .shift(controller_1_shr), .in(Q_out), .clk(CLKt), .clr(controller_1_cl__a__q_1), .q0(Q__1_q0));  // open: out, load, d0
  _28biit_ALU u_28biit_alu_1 (
    .A(A_output), .B(M_q27), .Result(n28biit_alu_1_result), .Control0(controller_1_c0),
    .Control1(controller_1_c1));  // open: Zero, Negative, Overflow, Carry
endmodule

// 28-bit AND
module _28_bit_and (
  input  [27:0] A,
  input  [27:0] B,
  output [27:0] Result
);

  assign Result = A & B;  // AND_Gate and_1, 28 bits wide
endmodule

// 28-bit OR
module _28_bit_OR (
  input  [27:0] A,
  input  [27:0] B,
  output [27:0] Result
);

  assign Result = A | B;  // OR_Gate or_1, 28 bits wide
endmodule

module Full_adder (
  input  Carry_in,
  input  A,
  input  B,
  output Result,
  output Carry_out
);

  wire and_1_out, and_2_out, xor_1_out;

  and and_1 (and_1_out, B, A);
  xor xor_1 (xor_1_out, A, B);
  or or_1 (Carry_out, and_1_out, and_2_out);
  and and_2 (and_2_out, xor_1_out, Carry_in);
  xor xor_2 (Result, Carry_in, xor_1_out);
endmodule

// adder
module _28_bit_full_adder (
  input  Carry_in,
  input  [27:0] A,
  input  [27:0] B,
  output [27:0] Result,
  output Carry_out
);

  wire full_adder_1_p4, full_adder_2_p4, full_adder_3_p4, full_adder_4_p4, full_adder_5_p4, full_adder_6_p4,
       full_adder_7_p4, full_adder_8_p4, full_adder_9_p4, full_adder_10_p4, full_adder_11_p4,
       full_adder_12_p4, full_adder_13_p4, full_adder_14_p4, full_adder_15_p4, full_adder_16_p4,
       full_adder_17_p4, full_adder_18_p4, full_adder_19_p4, full_adder_20_p4, full_adder_21_p4,
       full_adder_22_p4, full_adder_23_p4, full_adder_24_p4, full_adder_25_p4, full_adder_26_p4,
       full_adder_27_p4;

  // _28_bit_ALU_Full_adder full_adder_1: pin names not known; wires that end beside it: B[0], A[0], Carry_in, full_adder_1_p4, Result[0]
  // _28_bit_ALU_Full_adder full_adder_2: pin names not known; wires that end beside it: B[1], A[1], full_adder_1_p4, full_adder_2_p4, Result[1]
  // _28_bit_ALU_Full_adder full_adder_3: pin names not known; wires that end beside it: B[2], A[2], full_adder_2_p4, full_adder_3_p4, Result[2]
  // _28_bit_ALU_Full_adder full_adder_4: pin names not known; wires that end beside it: B[3], A[3], full_adder_3_p4, full_adder_4_p4, Result[3]
  // _28_bit_ALU_Full_adder full_adder_5: pin names not known; wires that end beside it: A[4], B[4], full_adder_4_p4, full_adder_5_p4, Result[4]
  // _28_bit_ALU_Full_adder full_adder_6: pin names not known; wires that end beside it: A[5], B[5], full_adder_5_p4, full_adder_6_p4, Result[5]
  // _28_bit_ALU_Full_adder full_adder_7: pin names not known; wires that end beside it: A[6], B[6], full_adder_6_p4, full_adder_7_p4, Result[6]
  // _28_bit_ALU_Full_adder full_adder_8: pin names not known; wires that end beside it: A[7], B[7], full_adder_7_p4, full_adder_8_p4, Result[7]
  // _28_bit_ALU_Full_adder full_adder_9: pin names not known; wires that end beside it: A[8], B[8], full_adder_8_p4, full_adder_9_p4, Result[8]
  // _28_bit_ALU_Full_adder full_adder_10: pin names not known; wires that end beside it: A[9], B[9], full_adder_9_p4, full_adder_10_p4, Result[9]
  // _28_bit_ALU_Full_adder full_adder_11: pin names not known; wires that end beside it: A[10], B[10], full_adder_10_p4, full_adder_11_p4, Result[10]
  // _28_bit_ALU_Full_adder full_adder_12: pin names not known; wires that end beside it: A[11], B[11], full_adder_11_p4, full_adder_12_p4, Result[11]
  // _28_bit_ALU_Full_adder full_adder_13: pin names not known; wires that end beside it: A[12], B[12], full_adder_12_p4, full_adder_13_p4, Result[12]
  // _28_bit_ALU_Full_adder full_adder_14: pin names not known; wires that end beside it: A[13], B[13], full_adder_13_p4, full_adder_14_p4, Result[13]
  // _28_bit_ALU_Full_adder full_adder_15: pin names not known; wires that end beside it: A[14], B[14], full_adder_14_p4, full_adder_15_p4, Result[14]
  // _28_bit_ALU_Full_adder full_adder_16: pin names not known; wires that end beside it: A[15], B[15], full_adder_15_p4, full_adder_16_p4, Result[15]
  // _28_bit_ALU_Full_adder full_adder_17: pin names not known; wires that end beside it: A[16], B[16], full_adder_16_p4, full_adder_17_p4, Result[16]
  // _28_bit_ALU_Full_adder full_adder_18: pin names not known; wires that end beside it: A[17], B[17], full_adder_17_p4, full_adder_18_p4, Result[17]
  // _28_bit_ALU_Full_adder full_adder_19: pin names not known; wires that end beside it: A[18], B[18], full_adder_18_p4, full_adder_19_p4, Result[18]
  // _28_bit_ALU_Full_adder full_adder_20: pin names not known; wires that end beside it: A[19], B[19], full_adder_19_p4, full_adder_20_p4, Result[19]
  // _28_bit_ALU_Full_adder full_adder_21: pin names not known; wires that end beside it: A[20], B[21], full_adder_20_p4, full_adder_21_p4, Result[20]
  // _28_bit_ALU_Full_adder full_adder_22: pin names not known; wires that end beside it: A[21], B[20], full_adder_21_p4, full_adder_22_p4, Result[21]
  // _28_bit_ALU_Full_adder full_adder_23: pin names not known; wires that end beside it: A[22], B[22], full_adder_22_p4, full_adder_23_p4, Result[22]
  // _28_bit_ALU_Full_adder full_adder_24: pin names not known; wires that end beside it: A[23], B[23], full_adder_23_p4, full_adder_24_p4, Result[23]
  // _28_bit_ALU_Full_adder full_adder_25: pin names not known; wires that end beside it: A[24], B[24], full_adder_24_p4, full_adder_25_p4, Result[24]
  // _28_bit_ALU_Full_adder full_adder_26: pin names not known; wires that end beside it: A[25], B[25], full_adder_25_p4, full_adder_26_p4, Result[25]
  // _28_bit_ALU_Full_adder full_adder_27: pin names not known; wires that end beside it: A[26], B[26], full_adder_26_p4, full_adder_27_p4, Result[26]
  // _28_bit_ALU_Full_adder full_adder_28: pin names not known; wires that end beside it: A[27], B[27], full_adder_27_p4, Carry_out, Result[27]
endmodule

// xor
module _28_bit_xor (
  input  Control,
  input  [27:0] B,
  output [27:0] Result
);

  wire [27:0] bit_extender_1_out;

  assign bit_extender_1_out = {{27{Control}}, Control};  // Bit_Extender bit_extender_1
  assign Result = bit_extender_1_out ^ B;  // XOR_Gate xor_1, 28 bits wide
endmodule

// 32-bit \nADD/SUB
module Add_sub (
  input  Sub,
  input  [27:0] A,
  input  [27:0] B,
  output [27:0] Result,
  output Carry,
  output Overflow
);

  wire and_1_out, and_2_out, not_1_out, not_2_out, not_3_out, sign_bit_out_1_ms_bit, sign_bit_out_2_ms_bit,
       sign_bit_out_3_ms_bit;
  wire [27:0] n28_bit_xor_1_result;

  sign_bit_out sign_bit_out_1 (.Input(A), .MS_bit(sign_bit_out_1_ms_bit));
  not not_1 (not_1_out, sign_bit_out_1_ms_bit);
  _28_bit_xor u_28_bit_xor_1 (.B(B), .Result(n28_bit_xor_1_result), .Control(Sub));
  sign_bit_out sign_bit_out_2 (.Input(n28_bit_xor_1_result), .MS_bit(sign_bit_out_2_ms_bit));
  not not_2 (not_2_out, sign_bit_out_2_ms_bit);
  _28_bit_full_adder u_28_bit_full_adder_1 (
    .Carry_in(Sub), .A(A), .Result(Result), .Carry_out(Carry), .B(n28_bit_xor_1_result));
  sign_bit_out sign_bit_out_3 (.Input(Result), .MS_bit(sign_bit_out_3_ms_bit));
  not not_3 (not_3_out, sign_bit_out_3_ms_bit);
  and and_1 (and_1_out, not_3_out, sign_bit_out_2_ms_bit, sign_bit_out_1_ms_bit);
  and and_2 (and_2_out, sign_bit_out_3_ms_bit, not_2_out, not_1_out);
  or or_1 (Overflow, and_1_out, and_2_out);

  // Notes on the sheet:
  //   A31
  //   B31
  //   Result 31
endmodule

// 27th
module sign_bit_out (
  input  [27:0] Input,
  output MS_bit
);


  assign MS_bit = Input[27];
endmodule

// Reduce-OR
module _28_bit_reduce_or (
  input  [27:0] Input,
  output Output
);

  or or_1 (Output, Input[13], Input[0], Input[1], Input[2], Input[3], Input[4], Input[5], Input[6], Input[7], Input[8], Input[9], Input[10], Input[11], Input[12], Input[14], Input[15], Input[16], Input[17], Input[18], Input[19], Input[20], Input[21], Input[22], Input[23], Input[24], Input[25], Input[26], Input[27]);
endmodule

// 28 biit ALU
module _28biit_ALU (
  input  Control0,
  input  Control1,
  input  [27:0] A,
  input  [27:0] B,
  output [27:0] Result,
  output Zero,
  output Negative,
  output Overflow,
  output Carry
);

  wire n28_bit_reduce_or_1_output;
  wire [27:0] add_sub_1_result, multiplexer_1_out, n28_bit_and_1_result, n28_bit_or_1_result;

  _28_bit_and u_28_bit_and_1 (.A(A), .B(B), .Result(n28_bit_and_1_result));
  _28_bit_OR u_28_bit_or_1 (.A(A), .B(B), .Result(n28_bit_or_1_result));
  Add_sub add_sub_1 (.Sub(Control0), .A(A), .B(B), .Result(add_sub_1_result), .Carry(Carry), .Overflow(Overflow));
  Multiplexer #(.width(28), .enable("false")) multiplexer_1 (
    .in0(n28_bit_and_1_result), .in1(n28_bit_or_1_result), .out(multiplexer_1_out), .sel(Control0));
  Multiplexer #(.width(28), .enable("false")) multiplexer_2 (
    .in0(multiplexer_1_out), .in1(add_sub_1_result), .out(Result), .sel(Control1));
  sign_bit_out sign_bit_out_1 (.Input(Result), .MS_bit(Negative));
  _28_bit_reduce_or u_28_bit_reduce_or_1 (.Input(Result), .Output(n28_bit_reduce_or_1_output));
  not not_1 (Zero, n28_bit_reduce_or_1_output);
endmodule

// Control \nUnit
module Controller (
  input  Clk,
  input  Reset,
  input  Q0,
  input  Q_1,
  input  [4:0] Count,
  output Cl__A__Q_1,
  output LOad__M__Q__Cnt,
  output Load_A,
  output C0,
  output C1,
  output Shr,
  output Dec_Cnt
);

  wire and_3_out, multiplexer_1_out, not_1_out, not_2_out, not_3_out, not_4_out, not_5_out, not_6_out,
       not_7_out, or_2_out, Q0_prime_Q_1_out, Q0Q_1_prime_out;
  wire [1:0] rom_1_data_2;
  wire [2:0] and_1_out, and_2_out, bit_extender_1_out, bit_extender_2_out, bit_extender_3_out, CAR_q,
       or_1_out, rom_1_data;

  assign bit_extender_1_out = {{2{Q0_prime_Q_1_out}}, Q0_prime_Q_1_out};  // Bit_Extender bit_extender_1
  and Q0_prime_Q_1 (Q0_prime_Q_1_out, not_2_out, Q_1);
  not not_1 (not_1_out, Q0_prime_Q_1_out);
  assign bit_extender_2_out = {{2{not_1_out}}, not_1_out};  // Bit_Extender bit_extender_2
  assign and_1_out = 3'b100 & bit_extender_3_out & bit_extender_1_out;  // AND_Gate and_1, 3 bits wide
  assign or_1_out = and_1_out | rom_1_data | and_2_out;  // OR_Gate or_1, 3 bits wide
  not not_2 (not_2_out, Q0);
  assign and_2_out = bit_extender_2_out & bit_extender_3_out & 3'b101;  // AND_Gate and_2, 3 bits wide
  assign bit_extender_3_out = {{2{and_3_out}}, and_3_out};  // Bit_Extender bit_extender_3
  and and_3 (and_3_out, not_3_out, CAR_q[1], not_4_out);
  not not_3 (not_3_out, CAR_q[2]);
  not not_4 (not_4_out, CAR_q[0]);
  Counter #(.width(3), .max('h7)) CAR (
    .load(not_5_out), .D(or_1_out), .count(multiplexer_1_out), .Q(CAR_q), .clk(Clk), .clr(Reset));  // open: carry
  not not_5 (not_5_out, multiplexer_1_out);
  Multiplexer #(.select(2), .enable("false")) multiplexer_1 (
    .in0(1'b0), .in1(1'b1), .in2(Q0Q_1_prime_out), .in3(not_7_out), .out(multiplexer_1_out),
    .sel(rom_1_data_2));
  ROM #(.addrWidth(3), .dataWidth(12)) rom_1 (
    .addr(CAR_q), .data({Cl__A__Q_1, LOad__M__Q__Cnt, Load_A, C0, C1, Shr, Dec_Cnt, rom_1_data, rom_1_data_2}));  // open: sel
  and Q0Q_1_prime (Q0Q_1_prime_out, not_6_out, Q0);
  not not_6 (not_6_out, Q_1);
  not not_7 (not_7_out, or_2_out);
  or or_2 (or_2_out, Count[0], Count[1], Count[2], Count[3], Count[4]);

  // Notes on the sheet:
  //   To choose only
  //   state 2 (010)
  //   Control Word Format: Clear (A, Q-1), Load (M, Q, Cnt), Load A, C0, C1, Shr, Dec Cnt, Address bits (3 bit), Selection bits (2 bit)
  //   contents of rom_1 (hex, n*v repeats v):
  //   1 c01 2 394 281 61 b 1c
endmodule
